// Logisim project 24H_Format_Clock.circ as structural Verilog: 5 circuits, main circuit main
module main (
  input  Clear
);

  wire clock_1_out, n0_59_counter_1_next_clock, n0_59_counter_2_next_clock;
  wire [3:0] n0_23_counter_1_lsb, n0_23_counter_1_msb, n0_59_counter_1_lsb, n0_59_counter_1_msb,
       n0_59_counter_2_lsb, n0_59_counter_2_msb;

  Clock clock_1 (.out(clock_1_out));
  Hex_Digit_Display hex_digit_display_1 (.value(n0_23_counter_1_lsb));  // open: dp
  Hex_Digit_Display hex_digit_display_2 (.value(n0_23_counter_1_msb));  // open: dp
  _0_23_Counter u_0_23_counter_1 (
    .Clock(n0_59_counter_1_next_clock), .Clear(Clear), .MSB(n0_23_counter_1_msb), .LSB(n0_23_counter_1_lsb));  // open: Next_Clock
  Hex_Digit_Display hex_digit_display_3 (.value(n0_59_counter_1_msb));  // open: dp
  Hex_Digit_Display hex_digit_display_4 (.value(n0_59_counter_1_lsb));  // open: dp
  _0_59_counter u_0_59_counter_1 (
    .Clock(n0_59_counter_2_next_clock), .Clear(Clear), .MSB(n0_59_counter_1_msb), .LSB(n0_59_counter_1_lsb),
    .Next_Clock(n0_59_counter_1_next_clock));
  Hex_Digit_Display hex_digit_display_5 (.value(n0_59_counter_2_msb));  // open: dp
  Hex_Digit_Display hex_digit_display_6 (.value(n0_59_counter_2_lsb));  // open: dp
  _0_59_counter u_0_59_counter_2 (
    .Clock(clock_1_out), .Clear(Clear), .MSB(n0_59_counter_2_msb), .LSB(n0_59_counter_2_lsb),
    .Next_Clock(n0_59_counter_2_next_clock));
endmodule

module _0_59_counter (
  input  Clock,
  input  Clear,
  output [3:0] MSB,
  output [3:0] LSB,
  output Next_Clock
);

  wire _0_prime_out, _6_prime_out, decade_up_down_counter_1_a1_lsb, decade_up_down_counter_1_a2,
       decade_up_down_counter_1_a3, decade_up_down_counter_1_a4_msb, decade_up_down_counter_2_a1_lsb,
       decade_up_down_counter_2_a2, decade_up_down_counter_2_a3, decade_up_down_counter_2_a4_msb, not_1_out,
       not_2_out, not_3_out, not_4_out, not_5_out, not_6_out, not_7_out, nUP_out, or_1_out;

  not nUP (nUP_out, 1'b0);
  or or_1 (or_1_out, Clear, Next_Clock);
  and and_1 (Next_Clock, _0_prime_out, _6_prime_out);
  decade_up_down_counter decade_up_down_counter_1 (
    .Up1_down0(nUP_out), .Clear(or_1_out), .Clock(Clock), .A1_lsb(decade_up_down_counter_1_a1_lsb),
    .HEX(LSB), .A2(decade_up_down_counter_1_a2), .A3(decade_up_down_counter_1_a3),
    .A4_MSB(decade_up_down_counter_1_a4_msb));
  and _0_prime (_0_prime_out, not_1_out, not_2_out, not_3_out, not_5_out);
  not not_1 (not_1_out, decade_up_down_counter_1_a4_msb);
  not not_2 (not_2_out, decade_up_down_counter_1_a3);
  not not_3 (not_3_out, decade_up_down_counter_1_a2);
  not not_4 (not_4_out, decade_up_down_counter_1_a4_msb);
  not not_5 (not_5_out, decade_up_down_counter_1_a1_lsb);
  and _6_prime (_6_prime_out, not_6_out, decade_up_down_counter_2_a3, decade_up_down_counter_2_a2, not_7_out);
  not not_6 (not_6_out, decade_up_down_counter_2_a4_msb);
  decade_up_down_counter decade_up_down_counter_2 (
    .Up1_down0(nUP_out), .Clear(or_1_out), .Clock(not_4_out), .A1_lsb(decade_up_down_counter_2_a1_lsb),
    .HEX(MSB), .A2(decade_up_down_counter_2_a2), .A3(decade_up_down_counter_2_a3),
    .A4_MSB(decade_up_down_counter_2_a4_msb));
  not not_7 (not_7_out, decade_up_down_counter_2_a1_lsb);
  Hex_Digit_Display hex_digit_display_1 (.value(LSB));  // open: dp
  Hex_Digit_Display hex_digit_display_2 (.value(MSB));  // open: dp
endmodule

module decade_up_down_counter (
  input  Up1_down0,
  input  Clear,
  input  Clock,
  output A1_lsb,
  output [3:0] HEX,
  output A2,
  output A3,
  output A4_MSB
);

  wire and_1_out, and_2_out, and_3_out, and_4_out, and_5_out, and_6_out, Clear_out, j_k_ff_1_qn, j_k_ff_2_qn,
       j_k_ff_3_qn, not_1_out, or_1_out, or_2_out, or_3_out, or_4_out, or_5_out, or_6_out, or_7_out,
       Preset_out;

  not not_1 (not_1_out, Up1_down0);
  and and_1 (and_1_out, A1_lsb, Up1_down0);
  and and_2 (and_2_out, j_k_ff_1_qn, not_1_out);
  and and_3 (and_3_out, j_k_ff_2_qn, and_2_out);
  and and_4 (and_4_out, A3, and_6_out);
  and and_5 (and_5_out, j_k_ff_3_qn, and_3_out);
  or or_1 (or_1_out, Up1_down0, not_1_out);
  or or_2 (or_2_out, and_1_out, and_2_out);
  and and_6 (and_6_out, and_1_out, A2);
  or or_3 (or_3_out, and_6_out, and_3_out);
  or or_4 (or_4_out, and_4_out, and_5_out);
  or or_5 (or_5_out, Clear_out, Clear);
  J_K_Flip_Flop j_k_ff_1 (
    .J(or_1_out), .clk(Clock), .K(or_1_out), .Q(A1_lsb), .Qn(j_k_ff_1_qn), .preset(Preset_out),
    .reset(or_5_out));  // open: en
  J_K_Flip_Flop j_k_ff_2 (
    .J(or_2_out), .clk(Clock), .K(or_2_out), .Q(A2), .Qn(j_k_ff_2_qn), .reset(or_6_out));  // open: preset, en
  or or_6 (or_6_out, or_5_out, Preset_out);
  J_K_Flip_Flop j_k_ff_3 (
    .J(or_3_out), .clk(Clock), .K(or_3_out), .Q(A3), .Qn(j_k_ff_3_qn), .reset(or_7_out));  // open: preset, en
  or or_7 (or_7_out, or_5_out, Preset_out);
  J_K_Flip_Flop j_k_ff_4 (
    .J(or_4_out), .clk(Clock), .K(or_4_out), .Q(A4_MSB), .preset(Preset_out), .reset(or_5_out));  // open: Qn, en
  and u_Clear (Clear_out, Clock, j_k_ff_3_qn, A2, j_k_ff_1_qn, A4_MSB);
  and Preset (Preset_out, Clock, A1_lsb, A2, A3, A4_MSB);
  Hex_Digit_Display hex_digit_display_1 (.value({A4_MSB, A3, A2, A1_lsb}), .dp(1'b0));

  assign HEX = {A4_MSB, A3, A2, A1_lsb};
endmodule

module _24_clock (
  input  Clear
);

  wire clock_1_out, n0_59_counter_1_next_clock, n0_59_counter_2_next_clock;
  wire [3:0] n0_23_counter_1_lsb, n0_23_counter_1_msb, n0_59_counter_1_lsb, n0_59_counter_1_msb,
       n0_59_counter_2_lsb, n0_59_counter_2_msb;

  Clock clock_1 (.out(clock_1_out));
  Hex_Digit_Display hex_digit_display_1 (.value(n0_23_counter_1_lsb));  // open: dp
  Hex_Digit_Display hex_digit_display_2 (.value(n0_23_counter_1_msb));  // open: dp
  _0_23_Counter u_0_23_counter_1 (
    .Clock(n0_59_counter_1_next_clock), .Clear(Clear), .MSB(n0_23_counter_1_msb), .LSB(n0_23_counter_1_lsb));  // open: Next_Clock
  Hex_Digit_Display hex_digit_display_3 (.value(n0_59_counter_1_msb));  // open: dp
  Hex_Digit_Display hex_digit_display_4 (.value(n0_59_counter_1_lsb));  // open: dp
  _0_59_counter u_0_59_counter_1 (
    .Clock(n0_59_counter_2_next_clock), .Clear(Clear), .MSB(n0_59_counter_1_msb), .LSB(n0_59_counter_1_lsb),
    .Next_Clock(n0_59_counter_1_next_clock));
  Hex_Digit_Display hex_digit_display_5 (.value(n0_59_counter_2_msb));  // open: dp
  Hex_Digit_Display hex_digit_display_6 (.value(n0_59_counter_2_lsb));  // open: dp
  _0_59_counter u_0_59_counter_2 (
    .Clock(clock_1_out), .Clear(Clear), .MSB(n0_59_counter_2_msb), .LSB(n0_59_counter_2_lsb),
    .Next_Clock(n0_59_counter_2_next_clock));
endmodule

module _0_23_Counter (
  input  Clock,
  input  Clear,
  output [3:0] MSB,
  output [3:0] LSB,
  output Next_Clock
);

  wire _2_prime_out, _4_prime_out, decade_up_down_counter_1_a1_lsb, decade_up_down_counter_1_a2,
       decade_up_down_counter_1_a3, decade_up_down_counter_1_a4_msb, decade_up_down_counter_2_a1_lsb,
       decade_up_down_counter_2_a2, decade_up_down_counter_2_a3, decade_up_down_counter_2_a4_msb, not_1_out,
       not_2_out, not_3_out, not_4_out, not_5_out, not_6_out, not_7_out, nUP_out, or_1_out;

  not nUP (nUP_out, 1'b0);
  or or_1 (or_1_out, Clear, Next_Clock);
  and and_1 (Next_Clock, _4_prime_out, _2_prime_out);
  decade_up_down_counter decade_up_down_counter_1 (
    .Up1_down0(nUP_out), .Clear(or_1_out), .Clock(Clock), .A1_lsb(decade_up_down_counter_1_a1_lsb),
    .HEX(LSB), .A2(decade_up_down_counter_1_a2), .A3(decade_up_down_counter_1_a3),
    .A4_MSB(decade_up_down_counter_1_a4_msb));
  and _4_prime (_4_prime_out, not_1_out, decade_up_down_counter_1_a3, not_2_out, not_4_out);
  not not_1 (not_1_out, decade_up_down_counter_1_a4_msb);
  not not_2 (not_2_out, decade_up_down_counter_1_a2);
  not not_3 (not_3_out, decade_up_down_counter_1_a4_msb);
  not not_4 (not_4_out, decade_up_down_counter_1_a1_lsb);
  and _2_prime (_2_prime_out, not_5_out, not_7_out, decade_up_down_counter_2_a2, not_6_out);
  not not_5 (not_5_out, decade_up_down_counter_2_a4_msb);
  decade_up_down_counter decade_up_down_counter_2 (
    .Up1_down0(nUP_out), .Clear(or_1_out), .Clock(not_3_out), .A1_lsb(decade_up_down_counter_2_a1_lsb),
    .HEX(MSB), .A2(decade_up_down_counter_2_a2), .A3(decade_up_down_counter_2_a3),
    .A4_MSB(decade_up_down_counter_2_a4_msb));
  not not_6 (not_6_out, decade_up_down_counter_2_a1_lsb);
  not not_7 (not_7_out, decade_up_down_counter_2_a3);
  Hex_Digit_Display hex_digit_display_1 (.value(MSB));  // open: dp
  Hex_Digit_Display hex_digit_display_2 (.value(LSB));  // open: dp
endmodule
